# Fritzing sketch BasicCircuit (saved by Fritzing 0.9.2b)
breadboards: 1

parts:
  R1 = Resistor [tolerance=±5% resistance=220 package="1206 [SMD]"]
  LED1 = smd LED [color="Red (633nm)" package="0603 [SMD]"]
  Raspberry_Pi1 = Raspberry Pi B rev2

nets:
  N1: R1.Pin_0, Raspberry_Pi1.GND
  N2: R1.Pin_1, LED1.cathode
  N3: LED1.anode, Raspberry_Pi1.GPIO_18
