# Fritzing sketch ButtonDiagram (saved by Fritzing 0.9.2b)
breadboards: 1

parts:
  Raspberry_Pi1 = Raspberry Pi B rev2
  S1 = Pushbutton [package="[SMD]"]
  R1 = Resistor [tolerance=±5% resistance=4.7k package="2010 [SMD]"]
  LED1 = smd LED [color="Red (633nm)" package="0805 [SMD]"]
  R2 = Resistor [tolerance=±5% resistance=330 package="2010 [SMD]"]

nets:
  N1: Raspberry_Pi1.GND, S1.Pin_1, S1.Pin_2, R2.Pin_0
  N2: Raspberry_Pi1.GPIO_18, LED1.anode
  N3: Raspberry_Pi1.GPIO_25, S1.Pin_3, S1.Pin_4, R1.Pin_1
  N4: LED1.cathode, R2.Pin_1
